// Logisim project Single_cycle_block.circ as structural Verilog: 1 circuit, main circuit main
module main (
);

  wire ALU_SRC, clock_1_out, EXT_OP, SSET, WB;
  wire [1:0] Rd_SRC;
  wire [4:0] multiplexer_1_out;
  wire [9:0] undriven_2;
  wire [15:0] imm16, main_2_instruction;
  wire [19:0] PC_Plus_1;
  wire [31:0] alu_1_alu_result, bit_extender_1_out, bit_extender_2_out, main_3_bus_a, main_4_data_out,
       multiplexer_2_out, multiplexer_3_out, multiplexer_4_out, multiplexer_5_out, RS2, undriven;

  Clock clock_1 (.out(clock_1_out));
  pc_new_main main_1 (.PC_Output(PC_Plus_1), .Clk(clock_1_out));  // open: Pc_Selctor, Imm16, RS1, Immu, ImmL
  Instruction_Mem_main main_2 (.Address(PC_Plus_1), .Instruction({imm16, main_2_instruction}));
  assign bit_extender_1_out = {{16{imm16[15]}}, imm16};  // Bit_Extender bit_extender_1
  assign bit_extender_2_out = {{16{1'b0}}, imm16};  // Bit_Extender bit_extender_2
  Multiplexer #(.width(5), .enable("false")) multiplexer_1 (
    .in0(imm16[4:0]), .in1(main_2_instruction[10:6]), .out(multiplexer_1_out), .sel(SSET));
  Multiplexer #(.width(32), .enable("false")) multiplexer_2 (
    .in0(bit_extender_1_out), .in1(bit_extender_2_out), .out(multiplexer_2_out), .sel(EXT_OP));
  regfile_new_main main_3 (
    .Ra(main_2_instruction[15:11]), .Rb(multiplexer_1_out), .Rw(main_2_instruction[10:6]),
    .Bus_W(multiplexer_3_out), .Bus_A(main_3_bus_a), .Bus_B(RS2), .Clk(clock_1_out));  // open: Reg_write, R1, R2, R3, R4, R0, R5, R6, R7, R8, R9, R10, R11, R12, R13, R14, R15, R16, R17, R18, R19, R20, R21, R22, R23, R24, R25, R26, R27, R28, R29, R30, R31
  Multiplexer #(.select(2), .width(32), .enable("false")) multiplexer_3 (
    .in0({RS2[15:0], imm16}), .in1(multiplexer_2_out), .in2(multiplexer_5_out), .in3(undriven),
    .out(multiplexer_3_out), .sel(Rd_SRC));
  Bit_Extender #(.in_width(32), .out_width(20)) bit_extender_3 (.in(undriven), .out(PC_Plus_1));
  Multiplexer #(.width(32), .enable("false")) multiplexer_4 (
    .in0(multiplexer_2_out), .in1(RS2), .out(multiplexer_4_out), .sel(ALU_SRC));
  ALU alu_1 (
    .ALU_Result(alu_1_alu_result), .A(main_3_bus_a), .B(multiplexer_4_out), .ALU_Opration(undriven_2));  // open: less_flag_unsign, Overflow, less_flag, Zero_flag
  Data_Mem_main main_4 (
    .Clk(clock_1_out), .Data_In(RS2), .Data_Out(main_4_data_out), .Alu_Result(alu_1_alu_result));  // open: Mem_Write, Mem_Read
  Multiplexer #(.width(32), .enable("false")) multiplexer_5 (
    .in0(alu_1_alu_result), .in1(main_4_data_out), .out(multiplexer_5_out), .sel(WB));

  // Notes on the sheet:
  //   op_code
  //   function
  //   0-> SSET
  //   01-> SET
  //   10->ALU_Result
  //   imm16
endmodule
